// Logisim project new_arc.circ as structural Verilog: 7 circuits, main circuit main
module main (
  input  in_1,
  input  in_2,
  input  [7:0] in_3,
  output [7:0] out_4
);

  wire [7:0] n8bit_reg_1_out_5, n8bit_reg_2_out_5, undriven;

  _8bit_counter u_8bit_counter_1 (.count(in_1), .inp_en(in_2), .in_3(in_3), .out_4(out_4));
  _8bit_reg u_8bit_reg_1 (.in_1(undriven), .out_5(n8bit_reg_1_out_5));  // open: clk, select, out_6, out_enable
  _8bit_reg u_8bit_reg_2 (.in_1(undriven), .out_5(n8bit_reg_2_out_5));  // open: clk, select, out_6, out_enable
  ALU alu_1 (.in_1(n8bit_reg_1_out_5), .in_3(n8bit_reg_2_out_5));  // open: out_4, in_2
endmodule

module _8bit_reg (
  input  [7:0] in_1,
  input  clk,
  input  select,
  input  out_enable,
  output [7:0] out_5,
  output [7:0] out_6
);

  wire and_1_out;

  and and_1 (and_1_out, clk, select);
  D_Flip_Flop #(.trigger("falling")) d_ff_1 (
    .clk(and_1_out), .D(in_1[0]), .Q(out_5[0]));  // open: Qn, preset, en, reset
  D_Flip_Flop #(.trigger("falling")) d_ff_2 (
    .clk(and_1_out), .D(in_1[1]), .Q(out_5[1]));  // open: Qn, preset, en, reset
  D_Flip_Flop #(.trigger("falling")) d_ff_3 (
    .clk(and_1_out), .D(in_1[2]), .Q(out_5[2]));  // open: Qn, preset, en, reset
  D_Flip_Flop #(.trigger("falling")) d_ff_4 (
    .clk(and_1_out), .D(in_1[3]), .Q(out_5[3]));  // open: Qn, preset, en, reset
  D_Flip_Flop #(.trigger("falling")) d_ff_5 (
    .clk(and_1_out), .D(in_1[4]), .Q(out_5[4]));  // open: Qn, preset, en, reset
  D_Flip_Flop #(.trigger("falling")) d_ff_6 (
    .clk(and_1_out), .D(in_1[5]), .Q(out_5[5]));  // open: Qn, preset, en, reset
  D_Flip_Flop #(.trigger("falling")) d_ff_7 (
    .clk(and_1_out), .D(in_1[6]), .Q(out_5[6]));  // open: Qn, preset, en, reset
  D_Flip_Flop #(.trigger("falling")) d_ff_8 (
    .clk(and_1_out), .D(in_1[7]), .Q(out_5[7]));  // open: Qn, preset, en, reset
  assign out_6 = out_enable ? out_5 : 8'bz;  // Controlled_Buffer controlled_buffer_1
endmodule

module ALU (
  input  [7:0] in_1,
  input  [6:0] in_2,
  input  [7:0] in_3,
  output [7:0] out_4
);

  wire [7:0] adder_1_out, and_1_out, controled_inv_1_out_3, controled_inv_2_out_3, controled_inv_3_out_3,
       multiplexer_1_out, multiplexer_2_out, multiplexer_3_out;

  controled_inv controled_inv_1 (.in_1(multiplexer_1_out), .in_2(in_2[1]), .out_3(controled_inv_1_out_3));
  Multiplexer #(.width(8), .enable("false")) multiplexer_1 (
    .in0(in_1), .in1({8{1'b0}}), .out(multiplexer_1_out), .sel(in_2[0]));
  controled_inv controled_inv_2 (.in_1(multiplexer_2_out), .in_2(in_2[3]), .out_3(controled_inv_2_out_3));
  Multiplexer #(.width(8), .enable("false")) multiplexer_2 (
    .in0(in_3), .in1({8{1'b0}}), .out(multiplexer_2_out), .sel(in_2[2]));
  Adder adder_1 (.a(controled_inv_1_out_3), .b(controled_inv_2_out_3), .out(adder_1_out));  // open: cin, cout
  assign and_1_out = controled_inv_1_out_3 & controled_inv_2_out_3;  // AND_Gate and_1, 8 bits wide
  Multiplexer #(.width(8), .enable("false")) multiplexer_3 (
    .in0(adder_1_out), .in1(and_1_out), .out(multiplexer_3_out), .sel(in_2[5]));
  controled_inv controled_inv_3 (.in_1(multiplexer_3_out), .in_2(in_2[4]), .out_3(controled_inv_3_out_3));
  assign out_4 = in_2[6] ? controled_inv_3_out_3 : 8'bz;  // Controlled_Buffer controlled_buffer_1

  // Notes on the sheet:
  //   X
  //   Z x
  //   INV X
  //   Y
  //   Z y
  //   INV Y
  //   INV out
  //   X+Y||X&Y
  //   0           1
endmodule

module controled_inv (
  input  [7:0] in_1,
  input  in_2,
  output [7:0] out_3
);

  xor xor_1 (out_3[0], in_1[0], in_2);
  xor xor_2 (out_3[1], in_1[1], in_2);
  xor xor_3 (out_3[2], in_1[2], in_2);
  xor xor_4 (out_3[3], in_1[3], in_2);
  xor xor_5 (out_3[4], in_1[4], in_2);
  xor xor_6 (out_3[5], in_1[5], in_2);
  xor xor_7 (out_3[6], in_1[6], in_2);
  xor xor_8 (out_3[7], in_1[7], in_2);
endmodule

module _8bit_counter (
  input  count,
  input  inp_en,
  input  [7:0] in_3,
  output [7:0] out_4
);

  wire d_ff_1_qn, d_ff_2_qn, d_ff_3_qn, d_ff_4_qn, d_ff_5_qn, d_ff_6_qn, d_ff_7_qn, d_ff_8_qn,
       multiplexer_1_out, multiplexer_2_out, multiplexer_3_out, multiplexer_4_out, multiplexer_5_out,
       multiplexer_6_out, multiplexer_7_out, multiplexer_8_out, multiplexer_9_out, multiplexer_10_out,
       multiplexer_11_out, multiplexer_12_out, multiplexer_13_out, multiplexer_14_out, multiplexer_15_out,
       multiplexer_16_out;

  Multiplexer #(.enable("false")) multiplexer_1 (.in0(count), .in1(count), .out(multiplexer_1_out), .sel(inp_en));
  Multiplexer #(.enable("false")) multiplexer_2 (.in0(d_ff_1_qn), .in1(in_3[0]), .out(multiplexer_2_out), .sel(inp_en));
  Multiplexer #(.enable("false")) multiplexer_3 (.in0(out_4[0]), .in1(count), .out(multiplexer_3_out), .sel(inp_en));
  Multiplexer #(.enable("false")) multiplexer_4 (.in0(d_ff_2_qn), .in1(in_3[1]), .out(multiplexer_4_out), .sel(inp_en));
  Multiplexer #(.enable("false")) multiplexer_5 (.in0(out_4[1]), .in1(count), .out(multiplexer_5_out), .sel(inp_en));
  Multiplexer #(.enable("false")) multiplexer_6 (.in0(d_ff_3_qn), .in1(in_3[2]), .out(multiplexer_6_out), .sel(inp_en));
  Multiplexer #(.enable("false")) multiplexer_7 (.in0(out_4[2]), .in1(count), .out(multiplexer_7_out), .sel(inp_en));
  Multiplexer #(.enable("false")) multiplexer_8 (.in0(d_ff_4_qn), .in1(in_3[3]), .out(multiplexer_8_out), .sel(inp_en));
  Multiplexer #(.enable("false")) multiplexer_9 (.in0(out_4[3]), .in1(count), .out(multiplexer_9_out), .sel(inp_en));
  Multiplexer #(.enable("false")) multiplexer_10 (
    .in0(d_ff_5_qn), .in1(in_3[4]), .out(multiplexer_10_out), .sel(inp_en));
  Multiplexer #(.enable("false")) multiplexer_11 (.in0(out_4[4]), .in1(count), .out(multiplexer_11_out), .sel(inp_en));
  Multiplexer #(.enable("false")) multiplexer_12 (
    .in0(d_ff_6_qn), .in1(in_3[5]), .out(multiplexer_12_out), .sel(inp_en));
  Multiplexer #(.enable("false")) multiplexer_13 (.in0(out_4[5]), .in1(count), .out(multiplexer_13_out), .sel(inp_en));
  Multiplexer #(.enable("false")) multiplexer_14 (
    .in0(d_ff_7_qn), .in1(in_3[6]), .out(multiplexer_14_out), .sel(inp_en));
  Multiplexer #(.enable("false")) multiplexer_15 (.in0(out_4[6]), .in1(count), .out(multiplexer_15_out), .sel(inp_en));
  Multiplexer #(.enable("false")) multiplexer_16 (
    .in0(d_ff_8_qn), .in1(in_3[7]), .out(multiplexer_16_out), .sel(inp_en));
  D_Flip_Flop #(.trigger("falling")) d_ff_1 (
    .clk(multiplexer_1_out), .D(multiplexer_2_out), .Q(out_4[0]), .Qn(d_ff_1_qn));  // open: preset, en, reset
  D_Flip_Flop #(.trigger("falling")) d_ff_2 (
    .clk(multiplexer_3_out), .D(multiplexer_4_out), .Q(out_4[1]), .Qn(d_ff_2_qn));  // open: preset, en, reset
  D_Flip_Flop #(.trigger("falling")) d_ff_3 (
    .clk(multiplexer_5_out), .D(multiplexer_6_out), .Q(out_4[2]), .Qn(d_ff_3_qn));  // open: preset, en, reset
  D_Flip_Flop #(.trigger("falling")) d_ff_4 (
    .clk(multiplexer_7_out), .D(multiplexer_8_out), .Q(out_4[3]), .Qn(d_ff_4_qn));  // open: preset, en, reset
  D_Flip_Flop #(.trigger("falling")) d_ff_5 (
    .clk(multiplexer_9_out), .D(multiplexer_10_out), .Q(out_4[4]), .Qn(d_ff_5_qn));  // open: preset, en, reset
  D_Flip_Flop #(.trigger("falling")) d_ff_6 (
    .clk(multiplexer_11_out), .D(multiplexer_12_out), .Q(out_4[5]), .Qn(d_ff_6_qn));  // open: preset, en, reset
  D_Flip_Flop #(.trigger("falling")) d_ff_7 (
    .clk(multiplexer_13_out), .D(multiplexer_14_out), .Q(out_4[6]), .Qn(d_ff_7_qn));  // open: preset, en, reset
  D_Flip_Flop #(.trigger("falling")) d_ff_8 (
    .clk(multiplexer_15_out), .D(multiplexer_16_out), .Q(out_4[7]), .Qn(d_ff_8_qn));  // open: preset, en, reset
endmodule

module _2bit_counter (
  input  in_1,
  input  in_2,
  output out_3,
  output out_4
);

  wire d_ff_1_q, d_ff_2_qn, d_ff_3_qn, not_1_out;

  D_Flip_Flop #(.trigger("falling")) d_ff_1 (
    .clk(in_1), .D(in_2), .Q(d_ff_1_q), .reset(not_1_out));  // open: Qn, preset, en
  not not_1 (not_1_out, in_2);
  D_Flip_Flop #(.trigger("falling")) d_ff_2 (
    .clk(in_1), .D(d_ff_2_qn), .Q(out_3), .Qn(d_ff_2_qn), .reset(d_ff_1_q));  // open: preset, en
  D_Flip_Flop #(.trigger("falling")) d_ff_3 (
    .clk(out_3), .D(d_ff_3_qn), .Q(out_4), .Qn(d_ff_3_qn), .reset(d_ff_1_q));  // open: preset, en
endmodule

module instruction_reg (
  input  [7:0] in_1,
  output [6:0] ALU_controll
);

  wire n2bit_counter_1_out_3, n2bit_counter_1_out_4, nand_1_out, not_1_out;
  wire [7:0] n8bit_reg_1_out_5, rom_2_data;
  wire [7:7] rom_1_data;

  _2bit_counter u_2bit_counter_1 (.out_3(n2bit_counter_1_out_3), .out_4(n2bit_counter_1_out_4));  // open: in_1, in_2
  nand nand_1 (nand_1_out, n2bit_counter_1_out_3, n2bit_counter_1_out_4);
  _8bit_reg u_8bit_reg_1 (
    .in_1(in_1), .clk(nand_1_out), .select(nand_1_out), .out_5(n8bit_reg_1_out_5));  // open: out_6, out_enable
  not not_1 (not_1_out, nand_1_out);
  ROM rom_1 (.addr(n8bit_reg_1_out_5), .data({rom_1_data[7], ALU_controll}), .sel(not_1_out));
  ROM rom_2 (.addr(n8bit_reg_1_out_5), .data(rom_2_data), .sel(not_1_out));

  // Notes on the sheet:
  //   control bus
endmodule
